# Fritzing sketch tailless-attiny (saved by Fritzing 0.9.6b)
breadboards: 1

parts:
  Receiver = IC, SIP package, 8 pins [chip_label=RX]
  2S_Lipo = DC Power [voltage=8.4V]
  J1 = Basic Servo
  J2 = Basic Servo
  Weathervane = POT [package=alps_pot]
  IC1 = IC, DIP package, 10 pins [chip_label=ATTiny85]
  R1 = Resistor [tolerance=±5% power=0.25W resistance=100k package=THT]
  R2 = Resistor [tolerance=±5% power=0.25W resistance=100k package=THT]

nets:
  N1: Receiver.pin2, Weathervane.E, IC1.pin1
  N2: Receiver.pin3, IC1.pin10
  N3: Receiver.pin4, IC1.pin9
  VCC: 2S_Lipo.V+, J1.vcc, J2.vcc, IC1.pin2
  N4: 2S_Lipo.V-, J2.gnd
  N5: J1.gnd, Weathervane.A, IC1.pin4, R1.Pin_1
  N6: J1.pulse, IC1.pin7
  N7: J2.pulse, IC1.pin6
  N8: Weathervane.S, R2.Pin_0
  N9: IC1.pin8, R1.Pin_0, R2.Pin_1
