# Fritzing sketch tailless-nano (saved by Fritzing 0.9.3b)
breadboards: 1

parts:
  Receiver = IC, SIP package, 8 pins [chip_label=RX]
  Nano1 = Arduino Nano v2.3
  2S_Lipo = DC Power [voltage=8.4V]
  J1 = Basic Servo
  J2 = Basic Servo
  Weathervane = POT [package=alps_pot]

nets:
  GND: Receiver.pin1, Nano1.GND, 2S_Lipo.V-, J1.gnd, J2.gnd, Weathervane.A
  N1: Receiver.pin2, Nano1.+5V, Weathervane.E
  N2: Receiver.pin4, Nano1.D2
  N3: Receiver.pin5, Nano1.D3
  N4: Nano1.D4, J2.pulse
  N5: Nano1.D5, J1.pulse
  N6: Nano1.A7, Weathervane.S
  VCC: Nano1.VIN, 2S_Lipo.V+, J1.vcc, J2.vcc
