# Fritzing sketch tailless-imu (saved by Fritzing 0.9.6b)
breadboards: 1

parts:
  Receiver = IC, SIP package, 8 pins [chip_label=RX]
  Nano1 = Arduino Nano v2.3
  2S_Lipo = DC Power [voltage=8.4V]
  J1 = Basic Servo
  J2 = Basic Servo
  MPU6050_Gyro = IC, SIP package, 8 pins [chip_label=GY-521]

nets:
  GND: Receiver.pin1, Nano1.GND, 2S_Lipo.V-, J1.gnd, J2.gnd, MPU6050_Gyro.pin2
  N1: Receiver.pin2, Nano1.+5V, MPU6050_Gyro.pin1
  N2: Receiver.pin3, Nano1.D8
  N3: Receiver.pin4, Nano1.D9
  N4: Nano1.D3, J2.pulse
  N5: Nano1.D4, J1.pulse
  N6: Nano1.A5, MPU6050_Gyro.pin3
  N7: Nano1.A4, MPU6050_Gyro.pin4
  VCC: Nano1.VIN, 2S_Lipo.V+, J1.vcc, J2.vcc
